// Logisim project MIDI_Keypad_Logic_Simulation.circ as structural Verilog: 1 circuit, main circuit MIDI_Keypad_Logic
module MIDI_Keypad_Logic (
  input  SW1,
  input  SW2,
  input  Encoder_A,
  input  Encoder_B,
  input  Slider,
  input  Touch_1,
  input  Touch_2,
  input  Touch_3,
  input  Touch_4,
  input  Touch_5,
  input  LED_DATA,
  input  D3_DOUT_D4_DIN,
  input  D4_DOUT_D5_DIN,
  input  D5_DOUT_D6_DIN,
  input  D6_DOUT_UNCONNECTED,
  output SWITCH1,
  output SWITCH2,
  output ENC1_A,
  output ENC1_B,
  output SLIDE1,
  output TOUCH1,
  output TOUCH2,
  output TOUCH3,
  output TOUCH4,
  output TOUCH5,
  output LED_DATA_PROBE,
  output D3_DOUT_D4_DIN_PROBE,
  output D4_DOUT_D5_DIN_PROBE,
  output D5_DOUT_D6_DIN_PROBE,
  output D6_DOUT_UNCONNECTED_PROBE
);


  assign D3_DOUT_D4_DIN_PROBE = D3_DOUT_D4_DIN;
  assign D4_DOUT_D5_DIN_PROBE = D4_DOUT_D5_DIN;
  assign D5_DOUT_D6_DIN_PROBE = D5_DOUT_D6_DIN;
  assign D6_DOUT_UNCONNECTED_PROBE = D6_DOUT_UNCONNECTED;
  assign ENC1_A = Encoder_A;
  assign ENC1_B = Encoder_B;
  assign LED_DATA_PROBE = LED_DATA;
  assign SLIDE1 = Slider;
  assign SWITCH1 = SW1;
  assign SWITCH2 = SW2;
  assign TOUCH1 = Touch_1;
  assign TOUCH2 = Touch_2;
  assign TOUCH3 = Touch_3;
  assign TOUCH4 = Touch_4;
  assign TOUCH5 = Touch_5;
endmodule
